// Logisim project ULA8bit.circ as structural Verilog: 3 circuits, main circuit main
module main (
  input  [7:0] in_1,
  input  [3:0] Seletor,
  input  Ativado,
  output out_4
);

  Multiplexer #(.select(4)) multiplexer_1 (
    .in0(in_1[0]), .in1(in_1[1]), .in2(in_1[2]), .in3(in_1[3]), .in4(in_1[4]), .in5(in_1[5]), .in6(in_1[6]),
    .in7(in_1[7]), .out(out_4), .sel(Seletor), .en(Ativado));  // open: in8, in9, in10, in11, in12, in13, in14, in15
endmodule

module Seletor (
  input  SHIFT_esquerda,
  input  SHIFT_direita,
  input  A,
  input  B,
  input  [3:0] Seletor,
  input  Carry_in,
  input  Carry_out,
  output S
);

  wire adder_1_cout, adder_1_out, and_1_out, and_2_out, multiplexer_1_out, nand_1_out, nor_1_out, not_1_out,
       not_2_out, or_1_out, subtractor_1_bout, subtractor_1_out, xor_1_out;

  and and_1 (and_1_out, A, B);
  or or_1 (or_1_out, A, B);
  not not_1 (not_1_out, A);
  not not_2 (not_2_out, B);
  nor nor_1 (nor_1_out, A, B);
  nand nand_1 (nand_1_out, A, B);
  xor xor_1 (xor_1_out, A, B);
  Adder #(.width(1)) adder_1 (.a(A), .b(B), .out(adder_1_out), .cin(Carry_in), .cout(adder_1_cout));
  Subtractor #(.width(1)) subtractor_1 (.a(A), .b(B), .out(subtractor_1_out), .bin(Carry_in), .bout(subtractor_1_bout));
  Multiplexer multiplexer_1 (.in0(not_1_out), .in1(not_2_out), .out(multiplexer_1_out), .sel(1'b1));  // open: en
  and and_2 (and_2_out, ~Seletor[3], Seletor[2], Seletor[1], Seletor[0]);  // AND_Gate
  Multiplexer #(.select(4)) multiplexer_2 (
    .in0(and_1_out), .in1(or_1_out), .in2(multiplexer_1_out), .in3(nor_1_out), .in4(nand_1_out),
    .in5(xor_1_out), .in6(adder_1_out), .in7(subtractor_1_out), .in8(SHIFT_esquerda), .in9(SHIFT_direita),
    .out(S), .sel(Seletor));  // open: in10, in11, in12, in13, in14, in15, en
  Multiplexer multiplexer_3 (
    .in0(adder_1_cout), .in1(subtractor_1_bout), .out(Carry_out), .sel(and_2_out));  // open: en

  // Notes on the sheet:
  //    0000 - AND- S0
  //   0001 - OR - S1
  //   0010 - NOT - S2
  //   0011 - NOR - S3
  //   0100 - NAND - S4
  //   0101 - XOR - S5
  //   0110 - SOMA - S6
  //   0111 - SUB - S7
endmodule

module ULA (
  input  [7:0] A,
  input  [7:0] S,
  input  [3:0] Seletor,
  input  [7:0] B,
  output out_5
);

  wire undriven, undriven_2, undriven_3, undriven_4, undriven_5, undriven_6;

  Seletor seletor_1 (
    .SHIFT_esquerda(A[6]), .A(A[7]), .B(B[7]), .Carry_in(undriven), .SHIFT_direita(1'b0), .S(S[7]),
    .Seletor(Seletor), .Carry_out(out_5));
  Seletor seletor_2 (
    .SHIFT_esquerda(A[4]), .A(A[5]), .B(B[5]), .Carry_in(undriven_2), .SHIFT_direita(A[6]), .S(S[5]),
    .Seletor(Seletor), .Carry_out(undriven_3));
  Seletor seletor_3 (
    .SHIFT_esquerda(A[5]), .A(A[6]), .B(B[6]), .Carry_in(undriven_3), .SHIFT_direita(A[6]), .S(S[6]),
    .Seletor(Seletor), .Carry_out(undriven));
  Seletor seletor_4 (
    .SHIFT_esquerda(A[3]), .A(A[4]), .B(B[4]), .Carry_in(undriven_4), .SHIFT_direita(A[5]), .S(S[4]),
    .Seletor(Seletor), .Carry_out(undriven_2));
  Seletor seletor_5 (
    .SHIFT_esquerda(A[2]), .A(A[3]), .B(B[3]), .Carry_in(B[3]), .SHIFT_direita(A[4]), .S(S[3]),
    .Seletor(Seletor), .Carry_out(undriven_4));
  Seletor seletor_6 (
    .SHIFT_esquerda(A[1]), .A(A[2]), .B(B[2]), .Carry_in(undriven_5), .SHIFT_direita(A[3]), .S(S[2]),
    .Seletor(Seletor), .Carry_out(B[3]));
  Seletor seletor_7 (
    .SHIFT_esquerda(A[0]), .A(A[1]), .B(B[1]), .Carry_in(undriven_6), .SHIFT_direita(A[2]), .S(S[1]),
    .Seletor(Seletor), .Carry_out(undriven_5));
  Seletor seletor_8 (
    .SHIFT_esquerda(1'b0), .A(A[0]), .B(B[0]), .Carry_in(1'b0), .SHIFT_direita(A[1]), .S(S[0]),
    .Seletor(Seletor), .Carry_out(undriven_6));
endmodule
