// Logisim project maquina-estados.circ as structural Verilog: 1 circuit, main circuit main
module main (
  input  Dir,
  output out_2,
  output out_3,
  output out_4,
  output out_5
);

  wire and_1_out, and_2_out, and_3_out, and_4_out, clock_1_out, d_ff_1_q, d_ff_1_qn, d_ff_2_q, d_ff_2_qn,
       not_1_out, or_1_out;

  not not_1 (not_1_out, Dir);
  Clock clock_1 (.out(clock_1_out));
  and and_1 (and_1_out, d_ff_1_qn, d_ff_2_qn, Dir);
  and and_2 (and_2_out, d_ff_1_qn, d_ff_2_q, not_1_out);
  and and_3 (and_3_out, d_ff_1_q, Dir, Dir);
  and and_4 (and_4_out, d_ff_1_q, d_ff_2_qn, not_1_out);
  or or_1 (or_1_out, and_1_out, and_2_out, and_3_out, and_4_out);
  and and_5 (out_2, d_ff_1_qn, d_ff_2_qn);
  and and_6 (out_3, d_ff_1_qn, d_ff_2_q);
  D_Flip_Flop d_ff_1 (.clk(clock_1_out), .D(or_1_out), .Q(d_ff_1_q), .Qn(d_ff_1_qn));  // open: preset, en, reset
  and and_7 (out_4, d_ff_1_q, d_ff_2_qn);
  D_Flip_Flop d_ff_2 (.clk(clock_1_out), .D(d_ff_2_qn), .Q(d_ff_2_q), .Qn(d_ff_2_qn));  // open: preset, en, reset
  and and_8 (out_5, d_ff_1_q, d_ff_2_q);
endmodule
