// Logisim project memoria8bit.circ as structural Verilog: 5 circuits, main circuit main
module main (
  input  [7:0] Entrada,
  input  [1:0] Enderec,
  input  Limpar,
  output [7:0] out_4
);

  wire clock_1_out;

  Clock clock_1 (.out(clock_1_out));
  RAM ram_1 (.Entrada(Entrada), .Enderec(Enderec), .\Saída (out_4), .Clock(clock_1_out), .Limpar(Limpar));
endmodule

module ram_1x2 (
  input  [1:0] in_1,
  input  Clock,
  input  Ligar,
  input  Limpar,
  output [1:0] out_5
);

  wire j_k_ff_1_q, j_k_ff_2_q, not_1_out, not_2_out;

  not not_1 (not_1_out, in_1[1]);
  J_K_Flip_Flop j_k_ff_1 (
    .J(in_1[1]), .clk(Clock), .K(not_1_out), .Q(j_k_ff_1_q), .en(Ligar), .reset(Limpar));  // open: Qn, preset
  not not_2 (not_2_out, in_1[0]);
  J_K_Flip_Flop j_k_ff_2 (
    .J(in_1[0]), .clk(Clock), .K(not_2_out), .Q(j_k_ff_2_q), .en(Ligar), .reset(Limpar));  // open: Qn, preset
  and and_1 (out_5[0], Ligar, j_k_ff_2_q);
  and and_2 (out_5[1], Ligar, j_k_ff_1_q);
endmodule

module RAM1X4 (
  input  clock,
  input  [7:0] in_2,
  input  Ligar,
  input  Desligar,
  output [7:0] Saida
);

  ram_1x2 ram_1x2_1 (.Clock(clock), .out_5(Saida[1:0]), .in_1(in_2[1:0]), .Ligar(Ligar), .Limpar(Desligar));
  ram_1x2 ram_1x2_2 (.Clock(clock), .out_5(Saida[3:2]), .in_1(in_2[3:2]), .Ligar(Ligar), .Limpar(Desligar));
  ram_1x2 ram_1x2_3 (.Clock(clock), .out_5(Saida[5:4]), .in_1(in_2[5:4]), .Ligar(Ligar), .Limpar(Desligar));
  ram_1x2 ram_1x2_4 (.Clock(clock), .out_5(Saida[7:6]), .in_1(in_2[7:6]), .Ligar(Ligar), .Limpar(Desligar));
endmodule

module RAM (
  input  Clock,
  input  [7:0] Entrada,
  input  [1:0] Enderec,
  input  Limpar,
  output [7:0] \Saída 
);

  wire seletor_1_out_2, seletor_1_out_3, seletor_1_out_4, seletor_1_out_5;
  wire [7:0] ram1x4_1_saida, ram1x4_2_saida, ram1x4_3_saida, ram1x4_4_saida;

  seletor seletor_1 (
    .in_1(Enderec), .out_2(seletor_1_out_2), .out_3(seletor_1_out_3), .out_4(seletor_1_out_4),
    .out_5(seletor_1_out_5));
  RAM1X4 ram1x4_1 (.in_2(Entrada), .Saida(ram1x4_1_saida), .clock(Clock), .Ligar(seletor_1_out_2), .Desligar(Limpar));
  RAM1X4 ram1x4_2 (.in_2(Entrada), .Saida(ram1x4_2_saida), .clock(Clock), .Ligar(seletor_1_out_4), .Desligar(Limpar));
  RAM1X4 ram1x4_3 (.in_2(Entrada), .Saida(ram1x4_3_saida), .clock(Clock), .Ligar(seletor_1_out_3), .Desligar(Limpar));
  RAM1X4 ram1x4_4 (.in_2(Entrada), .Saida(ram1x4_4_saida), .clock(Clock), .Ligar(seletor_1_out_5), .Desligar(Limpar));
  assign \Saída  = ram1x4_1_saida | ram1x4_3_saida | ram1x4_4_saida | ram1x4_2_saida;  // OR_Gate or_1, 8 bits wide
endmodule

module seletor (
  input  [1:0] in_1,
  output out_2,
  output out_3,
  output out_4,
  output out_5
);

  wire not_1_out, not_2_out, not_3_out, not_4_out;

  not not_1 (not_1_out, in_1[0]);
  not not_2 (not_2_out, in_1[1]);
  not not_3 (not_3_out, in_1[1]);
  not not_4 (not_4_out, in_1[0]);
  and and_1 (out_2, not_1_out, not_2_out);
  and and_2 (out_3, in_1[0], not_3_out);
  and and_3 (out_4, in_1[1], not_4_out);
  and and_4 (out_5, in_1[1], in_1[0]);
endmodule
