// Logisim project somador8bit.circ as structural Verilog: 4 circuits, main circuit main
module main (
  input  a,
  input  b,
  input  cin,
  output S,
  output out_5
);

  wire and_1_out, and_2_out, xor_1_out;

  xor xor_1 (xor_1_out, a, b);
  xor xor_2 (S, xor_1_out, cin);
  and and_1 (and_1_out, xor_1_out, cin);
  and and_2 (and_2_out, a, b);
  or or_1 (out_5, and_1_out, and_2_out);
endmodule

module somador_4_bits (
  input  b,
  input  a,
  input  a3,
  input  b3,
  input  a4,
  input  b4,
  input  a2,
  input  b2,
  input  cin,
  input  a7,
  input  b7,
  input  a8,
  input  b8,
  input  a5,
  input  b5,
  input  a6,
  input  b6,
  output out_18,
  output out_19,
  output out_20,
  output out_21,
  output out_22,
  output out_23,
  output out_24,
  output out_25
);

  wire main_1_out_5, main_2_out_5, main_3_out_5, main_4_out_5, main_5_out_5, main_6_out_5, main_7_out_5,
       main_8_out_5;

  main main_1 (.a(a), .b(b), .cin(cin), .S(out_21), .out_5(main_1_out_5));
  main main_2 (.a(a2), .b(b2), .cin(main_1_out_5), .S(out_20), .out_5(main_2_out_5));
  main main_3 (.a(a5), .b(b5), .cin(main_6_out_5), .S(out_25), .out_5(main_3_out_5));
  main main_4 (.a(a3), .b(b3), .cin(main_2_out_5), .S(out_19), .out_5(main_4_out_5));
  main main_5 (.a(a6), .b(b6), .cin(main_3_out_5), .S(out_24), .out_5(main_5_out_5));
  main main_6 (.a(a4), .b(b4), .cin(main_4_out_5), .S(out_18), .out_5(main_6_out_5));
  main main_7 (.a(a7), .b(b7), .cin(main_5_out_5), .S(out_23), .out_5(main_7_out_5));
  main main_8 (.a(a8), .b(b8), .cin(main_7_out_5), .S(out_22), .out_5(main_8_out_5));
  LED led_1 (.in(main_8_out_5));
endmodule

module somador8bitsAdiciona4 (
  input  d,
  input  c,
  input  b,
  input  a
);

  Adder adder_1 ();  // open: a, b, out, cin, cout
endmodule

module somador1bit (
  input  a,
  input  b,
  input  cin,
  output S,
  output out_5
);

  wire and_1_out, and_2_out, xor_1_out;

  xor xor_1 (xor_1_out, a, b);
  xor xor_2 (S, xor_1_out, cin);
  and and_1 (and_1_out, xor_1_out, cin);
  and and_2 (and_2_out, a, b);
  or or_1 (out_5, and_1_out, and_2_out);
endmodule
